# Fritzing sketch letrack (saved by Fritzing 1.0.4)

parts:
  IR_Receiver = TSOP312.., 314.. [package=THT]
  IR_Transmitter = smd LED [color="Red (633nm)" package="0805 [SMD]"]
  Mod2 = Passive Buzzer
  JP5 = Header 6 [package=molex-1x6-ra]
  LED2 = smd LED [color="Red (633nm)" package="0805 [SMD]"]
  IR_Receiver_2 = TSOP312.., 314.. [package=THT]
  Mod3 = Raspberry Pi Pico
  Led_Light = LTE-302 [package=lte-302]

nets:
  N1: IR_Receiver.GND, IR_Transmitter.anode, Mod2.-, LED2.anode, IR_Receiver_2.Data, Mod3.pin_3, Mod3.pin_8, Mod3.pin_18, Mod3.pin_23, Mod3.pin_33, Mod3.pin_38, Mod3.pin_42, Led_Light.A
  N2: IR_Receiver.Vs, JP5.5
  N3: IR_Receiver.Data, Mod3.pin_14
  N4: IR_Transmitter.cathode, JP5.2
  N5: Mod2.S, Mod3.pin_15
  N6: JP5.1, LED2.cathode
  N7: JP5.4, IR_Receiver_2.Vs
  N8: JP5.6, Mod3.pin_36
  N9: IR_Receiver_2.GND, Mod3.pin_16
  N10: Mod3.pin_9, Led_Light.C

custom parts:
  Raspberry Pi Pico: Raspberry Pi Pico. Based around the RP2040 microcontroller the Pico is a low cost microcontroller device bringing Raspberry Pi quality, cost, and easy of use to the microcontroller space. Jan 2021, Split part in to two versions: tht (this one) and SMD. This one will drill holes for a .1 in header in pcb to allow plugging in the module as well as providing pads to solder the module to the top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
